# Fritzing sketch Flameduino (saved by Fritzing 0.9.2b)
circuit board: 6.88566cm x 5.36311cm
breadboards: 1

parts:
  Flameduino_v1_0 = Arduino Uno (Rev3)
  VReg = Voltage Regulator - 5V [package="TO220 [THT]"]
  BIP373 = Basic FET P-Channel [package="TO220 [THT]"]
  Vin = Screw terminal - 2 pins [package=THT]
  Frequency = screw terminal, 3 pins
  Coil = screw terminal, 3 pins
  Activation = screw terminal, 3 pins
  Qinterrupt = NPN-Transistor [package="TO92 [THT]"]
  LED = LED - 5mm [color="Red (633nm)" package="5 mm [THT]"]
  Rled = Resistor [tolerance=±5% resistance=330 package=THT]
  Pad1 = Pad [width=12 height=18 connect=center]
  Pad2 = Pad [width=12 height=18 connect=center]
  JMP = male pin header, 2 pins [form="♂ (male)"]
  DAC = DIP - 6 pins [chip_label=IC package="DIP (Dual Inline) [THT]"]
  Vehicle = screw terminal, 5 pins
  Spare = double row male pin header, 10 pins [form="♂ (male)"]
  Interrupt = Screw terminal - 2 pins [package=THT]
  Rc = Resistor [tolerance=±5% resistance=330 package=THT]
  Ri = Resistor [tolerance=±5% resistance=1k package=THT]

nets:
  N1: Flameduino_v1_0.A0, Frequency.pin2
  N2: Flameduino_v1_0.A1, Vehicle.pin3
  N3: Flameduino_v1_0.A2, Vehicle.pin5
  N4: Flameduino_v1_0.A3, Vehicle.pin2
  N5: Flameduino_v1_0.A4/SDA, DAC.SDA
  N6: Flameduino_v1_0.A5/SCL, DAC.SCL
  N7: Flameduino_v1_0.D8, Coil.pin1
  N8: Flameduino_v1_0.D9_PWM, Spare.pin8
  N9: Flameduino_v1_0.D10_PWM/SS, Spare.pin9
  N10: Flameduino_v1_0.D11_PWM/MOSI, Ri.Pin_0
  N11: Flameduino_v1_0.D12/MISO, Spare.pin2
  N12: Flameduino_v1_0.D13/SCK, Rled.Pin_1
  GND: Flameduino_v1_0.GND, VReg.GND, BIP373.drain, Vin.pin1, Frequency.pin1, Qinterrupt.C, LED.cathode, Pad1.pad, Pad2.pad, DAC.Vss, Spare.pin10
  N13: Flameduino_v1_0.D0/RX, Spare.pin6
  N14: Flameduino_v1_0.D1/TX, Spare.pin7
  N15: Flameduino_v1_0.D2, Activation.pin2
  N16: Flameduino_v1_0.D3_PWM, Vehicle.pin1
  N17: Flameduino_v1_0.D4, Coil.pin2, JMP.pin1
  N18: Flameduino_v1_0.D5_PWM, Activation.pin3
  N19: Flameduino_v1_0.D6_PWM, Spare.pin3
  N20: Flameduino_v1_0.D7, Activation.pin1
  N21: Flameduino_v1_0.RESET, Spare.pin1
  5V: Flameduino_v1_0.5V, Frequency.pin3, DAC.Vdd, Spare.pin5
  N22: Flameduino_v1_0.VIN, VReg.output_voltage, Spare.pin4
  N23: VReg.input_voltage, Vin.pin2, Interrupt.pin2
  N24: BIP373.gate, Rc.Pin_1
  N25: BIP373.source, Coil.pin3
  N26: Qinterrupt.E, Interrupt.pin1
  N27: Qinterrupt.B, Ri.Pin_1
  N28: LED.anode, Rled.Pin_0
  N29: JMP.pin2, Rc.Pin_0
  N30: DAC.Vout, Vehicle.pin4

notes:
  © Eric Menze
  +
  -
  LED
  INT
  SRC
  Tach
  Trim
  MAFout
  MAPin
  O2in
  IATin
  +9V
  +12V
  Power -
  Logic +/-
  Static -/+
  E
  B
  C
  330Ω
  RST
  GND
  10
  12
  9
  6
  1
  0
  +5V
  1kΩ

custom parts:
  DIP - 6 pins: A DIP stand-in part for whatever IC you want. With 6 pins on a 300mil dual inline package (DIP) footprint.
